# Fritzing sketch WRDCLK_Anschlüsse (saved by Fritzing 0.9.2b)
breadboards: 1

parts:
  R1 = Resistor [tolerance=±20% resistance=1M package=THT]
  R2 = Resistor [tolerance=±5% resistance=10k package=THT]
  D1 = Rectifier Diode [part_number=1N4148 package="300 mil [THT]"]
  D2 = Rectifier Diode [part_number=1N4148 package="300 mil [THT]"]
  C1 = Ceramic Capacitor [capacitance=0.1nF package="100 mil [THT, multilayer]"]
  R4 = Resistor [tolerance=±5% resistance=330 package=THT]
  Arduino_Nano = Arduino Nano (Rev3.0)
  SENSOR_+5V = female pin header, 1 pin [form="♀ (female)"]  # not connected
  SENSOR_DATA1 = female pin header, 1 pin [form="♀ (female)"]  # not connected
  SENSOR_DATA2 = female pin header, 1 pin [form="♀ (female)"]  # not connected
  SENSOR_FÜHLER = female pin header, 1 pin [form="♀ (female)"]  # not connected
  SENSOR_GND = female pin header, 1 pin [form="♀ (female)"]  # not connected
  LED_+5V = female pin header, 1 pin [form="♀ (female)"]  # not connected
  LED_DI = female pin header, 1 pin [form="♀ (female)"]  # not connected
  LED_GND = female pin header, 1 pin [form="♀ (female)"]  # not connected
  DCF_+ = female pin header, 1 pin [form="♀ (female)"]  # not connected
  DCF_SIG = female pin header, 1 pin [form="♀ (female)"]  # not connected
  DCF_- = female pin header, 1 pin [form="♀ (female)"]  # not connected
  Micro_USB_In = USB Connectors [package=usb-microb]
  DS3231_VCC = female pin header, 1 pin [form="♀ (female)"]  # not connected
  DS3231_SCL = female pin header, 1 pin [form="♀ (female)"]  # not connected
  DS3231_GND = female pin header, 1 pin [form="♀ (female)"]  # not connected
  DS3231_SDA = female pin header, 1 pin [form="♀ (female)"]  # not connected
  R3 = Resistor [tolerance=±20% resistance=10k package=THT]
  D3 = Rectifier Diode [part_number=1N4148 package="300 mil [THT]"]

nets:
  Arduino D4: R1.Pin_0, Arduino_Nano.D4
  N1: R1.Pin_1, R2.Pin_0, C1.1, Arduino_Nano.D8
  Arduino D8/Sensorfeld: R2.Pin_1, D1.anode, D2.cathode
  +5V/DCF V IN / +5V/LED V IN / +5V/Vb +5V: D1.cathode, Arduino_Nano.VIN, Micro_USB_In.D+, R3.Pin_0, D3.cathode
  DCF GND/GND/LED GND: D2.anode, C1.0, Arduino_Nano.GND, Micro_USB_In.GND
  N2: R4.Pin_0, Arduino_Nano.D6
  LED DATA IN: R4.Pin_1, D3.anode
  DCF Signal: Arduino_Nano.D2, R3.Pin_1
  SCL: Arduino_Nano.A5
  SDA: Arduino_Nano.A4

notes:
  WRDCLK JEFD
